# Fritzing sketch heat_sensor_@_2_sides_fixed (saved by Fritzing 0.9.3b)
circuit board: 2.77087cm x 1.75758cm
breadboards: 1

parts:
  ESP01 = ESP8266 ESP01 [part_number=ESP8266 package=THT]
  X1 = USB Connectors 0000 [package=usb-a-h]
  DHT1 = DHT22 Humidity and Temperature Sensor
  C3 = Ceramic Capacitor [capacitance=0.1µF package="0805 [SMD, multilayer]"]
  C1 = Electrolytic Capacitor [capacitance=100µF package="100 mil [THT, electrolytic]"]
  U1 = l4931 [package=dpak]

nets:
  GND: ESP01.GND, X1.GND, DHT1.GND, C3.0, C1.-, U1.GND
  VCC: ESP01.VCC, ESP01.CH_PD, DHT1.VDD, C1.+, U1.OUT
  N1: ESP01.GPIO02, DHT1.DATA
  N2: X1.D+, C3.1, U1.IN

custom parts:
  ESP8266 ESP01: Generic WiFi Module based on the ESP8266 with onboard PCB antenna and UART communications
  USB Connectors 0000: USB Connectors USB-B-PTH is fully proven SKU : PRT-00139 USB-miniB is fully proven SKU : PRT-00587 USB-A-PCB is untested. USB-A-H is throughly reviewed, but untested. Spark Fun Electronics SKU : PRT-00437 USB-B-SMT is throughly reviewed, but untested. Needs silkscreen touching up. USB-A-S has not been used/tested USB-MB-H has not been used/tested
